// Logisim project exp_1_DHRUV.circ as structural Verilog
module main (
  input  [7:0] in_1,
  input  in_2,
  input  in_3,
  input  in_4,
  input  in_5,
  input  in_6,
  input  in_7,
  input  in_8,
  input  in_9
);

  wire bcd_to7_1_a0_2, bcd_to7_1_a1_2, bcd_to7_1_a2_2, bcd_to7_1_a3_2, bcd_to7_1_b0, bcd_to7_1_b1,
       bcd_to7_1_b2, bcd_to7_1_b3, n7_segment_1_a, n7_segment_1_b, n7_segment_1_c, n7_segment_1_d,
       n7_segment_1_e, n7_segment_1_f, n7_segment_1_g, n7_segment_2_a, n7_segment_2_b, n7_segment_2_c,
       n7_segment_2_d, n7_segment_2_e, n7_segment_2_f, n7_segment_2_g, n7_segment_3_a, n7_segment_3_b,
       n7_segment_3_c, n7_segment_3_d, n7_segment_3_e, n7_segment_3_f, n7_segment_3_g, n7_segment_4_a,
       n7_segment_4_b, n7_segment_4_c, n7_segment_4_d, n7_segment_4_e, n7_segment_4_f, n7_segment_4_g;

  _7_segment u_7_segment_1 (
    .A0(in_2), .A1(in_4), .A2(in_6), .A3(in_8), .A(n7_segment_1_a), .B(n7_segment_1_b), .C(n7_segment_1_c),
    .D(n7_segment_1_d), .E(n7_segment_1_e), .F(n7_segment_1_f), .G(n7_segment_1_g));
  _7_Segment_Display u_7_segment_display_1 (
    .g(n7_segment_1_g), .f(n7_segment_1_f), .a(n7_segment_1_a), .b(n7_segment_1_b), .e(n7_segment_1_e),
    .d(n7_segment_1_d), .c(n7_segment_1_c));  // open: dp
  bcd_to7 bcd_to7_1 (
    .a0(in_1[7]), .a1(in_1[6]), .a2(in_1[5]), .a3(in_1[4]), .a4(in_1[3]), .a5(in_1[2]), .a6(in_1[1]),
    .a7(in_1[0]), .A0_2(bcd_to7_1_a0_2), .A1_2(bcd_to7_1_a1_2), .A2_2(bcd_to7_1_a2_2), .A3_2(bcd_to7_1_a3_2),
    .B0(bcd_to7_1_b0), .B1(bcd_to7_1_b1), .B2(bcd_to7_1_b2), .B3(bcd_to7_1_b3));
  _7_segment u_7_segment_2 (
    .A0(bcd_to7_1_a0_2), .A1(bcd_to7_1_a1_2), .A2(bcd_to7_1_a2_2), .A3(bcd_to7_1_a3_2), .A(n7_segment_2_a),
    .B(n7_segment_2_b), .C(n7_segment_2_c), .D(n7_segment_2_d), .E(n7_segment_2_e), .F(n7_segment_2_f),
    .G(n7_segment_2_g));
  _7_segment u_7_segment_3 (
    .A0(bcd_to7_1_b0), .A1(bcd_to7_1_b1), .A2(bcd_to7_1_b2), .A3(bcd_to7_1_b3), .A(n7_segment_3_a),
    .B(n7_segment_3_b), .C(n7_segment_3_c), .D(n7_segment_3_d), .E(n7_segment_3_e), .F(n7_segment_3_f),
    .G(n7_segment_3_g));
  _7_Segment_Display u_7_segment_display_2 (
    .g(n7_segment_2_g), .f(n7_segment_2_f), .a(n7_segment_2_a), .b(n7_segment_2_b), .e(n7_segment_2_e),
    .d(n7_segment_2_d), .c(n7_segment_2_c));  // open: dp
  _7_segment u_7_segment_4 (
    .A0(in_3), .A1(in_5), .A2(in_7), .A3(in_9), .A(n7_segment_4_a), .B(n7_segment_4_b), .C(n7_segment_4_c),
    .D(n7_segment_4_d), .E(n7_segment_4_e), .F(n7_segment_4_f), .G(n7_segment_4_g));
  _7_Segment_Display u_7_segment_display_3 (
    .g(n7_segment_3_g), .f(n7_segment_3_f), .a(n7_segment_3_a), .b(n7_segment_3_b), .e(n7_segment_3_e),
    .d(n7_segment_3_d), .c(n7_segment_3_c));  // open: dp
  _7_Segment_Display u_7_segment_display_4 (
    .g(n7_segment_4_g), .f(n7_segment_4_f), .a(n7_segment_4_a), .b(n7_segment_4_b), .e(n7_segment_4_e),
    .d(n7_segment_4_d), .c(n7_segment_4_c));  // open: dp

  // Notes on the sheet:
  //   23CS041
endmodule

module bcd_to7 (
  input  a0,
  input  a1,
  input  a2,
  input  a3,
  input  a4,
  input  a5,
  input  a6,
  input  a7,
  output A0_2,
  output A1_2,
  output A2_2,
  output A3_2,
  output B0,
  output B1,
  output B2,
  output B3
);

  wire and_1_out, and_2_out, and_3_out, and_4_out, and_5_out, and_6_out, and_7_out, and_8_out, and_9_out,
       and_10_out, and_11_out, and_12_out, and_13_out, and_14_out, and_15_out, and_16_out, and_17_out,
       and_18_out, and_19_out, and_20_out, and_21_out, and_22_out, and_23_out, and_24_out, and_25_out,
       and_26_out, and_27_out, and_28_out, and_29_out, and_30_out, and_31_out, and_32_out, and_33_out,
       and_34_out, and_35_out, and_36_out, and_37_out, and_38_out, and_39_out, and_40_out, and_41_out,
       and_42_out, and_43_out, and_44_out, and_45_out, and_46_out, and_47_out, and_48_out, and_49_out,
       and_50_out, and_51_out, and_52_out, and_53_out, and_54_out, and_55_out, and_56_out, and_57_out,
       and_58_out, not_1_out, not_2_out, not_3_out, not_4_out, not_5_out, not_6_out, not_7_out, not_8_out,
       not_9_out, not_10_out, not_11_out, not_12_out, not_13_out, not_14_out, not_15_out, not_16_out,
       not_17_out, not_18_out, not_19_out, not_20_out, not_21_out, not_22_out, not_23_out, not_24_out,
       not_25_out, not_26_out, not_27_out, not_28_out, not_29_out, not_30_out, not_31_out, not_32_out,
       not_33_out, not_34_out, not_35_out, not_36_out, not_37_out, not_38_out, not_39_out, not_40_out,
       not_41_out, not_42_out, not_43_out, not_44_out, not_45_out, not_46_out, not_47_out, not_48_out,
       not_49_out, not_50_out, not_51_out, not_52_out, not_53_out, not_54_out, not_55_out, not_56_out,
       not_57_out, not_58_out, not_59_out, not_60_out, not_61_out, not_62_out, not_63_out, not_64_out,
       not_65_out, not_66_out, not_67_out, not_68_out, not_69_out, not_70_out, not_71_out, not_72_out,
       not_73_out, not_74_out, not_75_out, not_76_out, not_77_out, not_78_out, not_79_out, not_80_out,
       not_81_out, not_82_out, not_83_out, not_84_out, not_85_out, not_86_out, not_87_out, not_88_out,
       not_89_out, not_90_out, not_91_out, not_92_out, not_93_out, not_94_out, not_95_out, not_96_out,
       not_97_out, not_98_out, not_99_out, not_100_out, not_101_out, not_102_out, not_103_out, not_104_out,
       not_105_out, not_106_out, not_107_out, not_108_out, not_109_out, not_110_out, not_111_out,
       not_112_out, not_113_out, not_114_out, not_115_out;

  and and_1 (and_1_out, a1, a3);
  and and_2 (and_2_out, a1, a2);
  and and_3 (and_3_out, a2, a4);
  and and_4 (and_4_out, a2, a3);
  not not_1 (not_1_out, a2);
  and and_5 (and_5_out, a1, not_1_out, not_2_out);
  not not_2 (not_2_out, a3);
  not not_3 (not_3_out, a1);
  not not_4 (not_4_out, a2);
  not not_5 (not_5_out, a1);
  not not_6 (not_6_out, a2);
  not not_7 (not_7_out, a1);
  not not_8 (not_8_out, a1);
  not not_9 (not_9_out, a3);
  not not_10 (not_10_out, a4);
  not not_11 (not_11_out, a2);
  not not_12 (not_12_out, a3);
  not not_13 (not_13_out, a2);
  not not_14 (not_14_out, a3);
  not not_15 (not_15_out, a2);
  not not_16 (not_16_out, a3);
  not not_17 (not_17_out, a2);
  not not_18 (not_18_out, a1);
  not not_19 (not_19_out, a2);
  not not_20 (not_20_out, a4);
  not not_21 (not_21_out, a5);
  not not_22 (not_22_out, a3);
  not not_23 (not_23_out, a4);
  not not_24 (not_24_out, a4);
  not not_25 (not_25_out, a4);
  not not_26 (not_26_out, a5);
  not not_27 (not_27_out, a3);
  not not_28 (not_28_out, a3);
  not not_29 (not_29_out, a1);
  not not_30 (not_30_out, a2);
  not not_31 (not_31_out, a3);
  not not_32 (not_32_out, a5);
  not not_33 (not_33_out, a6);
  not not_34 (not_34_out, a1);
  not not_35 (not_35_out, a2);
  not not_36 (not_36_out, a4);
  not not_37 (not_37_out, a5);
  not not_38 (not_38_out, a1);
  not not_39 (not_39_out, a2);
  not not_40 (not_40_out, a6);
  not not_41 (not_41_out, a3);
  not not_42 (not_42_out, a4);
  not not_43 (not_43_out, a4);
  not not_44 (not_44_out, a5);
  not not_45 (not_45_out, a6);
  not not_46 (not_46_out, a5);
  not not_47 (not_47_out, a3);
  not not_48 (not_48_out, a4);
  not not_49 (not_49_out, a6);
  not not_50 (not_50_out, a3);
  not not_51 (not_51_out, a5);
  not not_52 (not_52_out, a6);
  not not_53 (not_53_out, a1);
  not not_54 (not_54_out, a2);
  not not_55 (not_55_out, a3);
  not not_56 (not_56_out, a4);
  not not_57 (not_57_out, a1);
  not not_58 (not_58_out, a3);
  not not_59 (not_59_out, a1);
  not not_60 (not_60_out, a2);
  not not_61 (not_61_out, a5);
  not not_62 (not_62_out, a6);
  not not_63 (not_63_out, a1);
  not not_64 (not_64_out, a2);
  not not_65 (not_65_out, a5);
  not not_66 (not_66_out, a1);
  not not_67 (not_67_out, a5);
  not not_68 (not_68_out, a6);
  not not_69 (not_69_out, a1);
  not not_70 (not_70_out, a3);
  not not_71 (not_71_out, a4);
  not not_72 (not_72_out, a5);
  not not_73 (not_73_out, a3);
  not not_74 (not_74_out, a6);
  not not_75 (not_75_out, a4);
  not not_76 (not_76_out, a3);
  not not_77 (not_77_out, a4);
  not not_78 (not_78_out, a5);
  not not_79 (not_79_out, a6);
  not not_80 (not_80_out, a2);
  not not_81 (not_81_out, a3);
  not not_82 (not_82_out, a5);
  not not_83 (not_83_out, a3);
  not not_84 (not_84_out, a6);
  not not_85 (not_85_out, a4);
  not not_86 (not_86_out, a2);
  not not_87 (not_87_out, a3);
  not not_88 (not_88_out, a4);
  not not_89 (not_89_out, a5);
  not not_90 (not_90_out, a1);
  not not_91 (not_91_out, a2);
  not not_92 (not_92_out, a4);
  not not_93 (not_93_out, a2);
  not not_94 (not_94_out, a3);
  not not_95 (not_95_out, a6);
  not not_96 (not_96_out, a1);
  not not_97 (not_97_out, a2);
  not not_98 (not_98_out, a4);
  not not_99 (not_99_out, a5);
  not not_100 (not_100_out, a6);
  not not_101 (not_101_out, a1);
  not not_102 (not_102_out, a2);
  not not_103 (not_103_out, a5);
  not not_104 (not_104_out, a3);
  not not_105 (not_105_out, a4);
  not not_106 (not_106_out, a6);
  not not_107 (not_107_out, a4);
  not not_108 (not_108_out, a6);
  not not_109 (not_109_out, a3);
  not not_110 (not_110_out, a5);
  not not_111 (not_111_out, a6);
  not not_112 (not_112_out, a3);
  not not_113 (not_113_out, a6);
  not not_114 (not_114_out, a6);
  not not_115 (not_115_out, a4);
  or or_1 (A0_2, and_1_out, and_2_out);
  or or_2 (A1_2, and_3_out, and_4_out, and_5_out);
  and and_6 (and_6_out, not_3_out, not_4_out, a3, a5);
  and and_7 (and_7_out, not_5_out, not_6_out, a3, a4);
  and and_8 (and_8_out, not_7_out, a3, a4, a5);
  and and_9 (and_9_out, not_8_out, a2, not_9_out, not_10_out);
  and and_10 (and_10_out, a1, not_11_out, not_12_out);
  and and_11 (and_11_out, not_13_out, not_14_out, a4, a6);
  and and_12 (and_12_out, not_15_out, not_16_out, a4, a5);
  and and_13 (and_13_out, not_17_out, a4, a5, a6);
  and and_14 (and_14_out, not_18_out, not_19_out, a3, not_20_out, not_21_out);
  and and_15 (and_15_out, a2, not_22_out, not_23_out);
  and and_16 (and_16_out, a2, not_24_out, a6);
  and and_17 (and_17_out, a2, not_25_out, a5);
  and and_18 (and_18_out, a2, a3, a4, not_26_out);
  and and_19 (and_19_out, a1, not_27_out, a5, a6);
  and and_20 (and_20_out, a1, not_28_out, a4);
  and and_21 (and_21_out, a1, a4, a6);
  and and_22 (and_22_out, a1, a4, a5);
  and and_23 (and_23_out, not_29_out, not_30_out, not_31_out, a4, not_32_out, not_33_out);
  and and_24 (and_24_out, not_34_out, not_35_out, a3, not_36_out, not_37_out, a6);
  and and_25 (and_25_out, not_38_out, not_39_out, a3, a4, a5, not_40_out);
  and and_26 (and_26_out, a2, not_41_out, not_42_out, a5, a6);
  and and_27 (and_27_out, a2, a3, not_43_out, not_44_out, not_45_out);
  and and_28 (and_28_out, a2, a3, a4, not_46_out, a6);
  and and_29 (and_29_out, a1, not_47_out, not_48_out, a5, not_49_out);
  and and_30 (and_30_out, a1, not_50_out, a4, a5, a6);
  and and_31 (and_31_out, a1, a3, a4, not_51_out, not_52_out);
  and and_32 (and_32_out, a1, a2, a6);
  and and_33 (and_33_out, not_53_out, not_54_out, not_55_out, not_56_out, a5);
  and and_34 (and_34_out, not_57_out, not_58_out, a4, a5, a6);
  and and_35 (and_35_out, not_59_out, not_60_out, a3, not_61_out, not_62_out);
  and and_36 (and_36_out, not_63_out, not_64_out, a3, a4, not_65_out);
  and and_37 (and_37_out, not_66_out, a3, a4, not_67_out, not_68_out);
  and and_38 (and_38_out, not_69_out, a2, not_70_out, not_71_out, not_72_out, a6);
  and and_39 (and_39_out, a2, not_73_out, a5, not_74_out);
  and and_40 (and_40_out, a2, a3, not_75_out, a5, a6);
  and and_41 (and_41_out, a1, not_76_out, not_77_out, not_78_out, not_79_out);
  and and_42 (and_42_out, a1, not_80_out, not_81_out, not_82_out, a6);
  and and_43 (and_43_out, a1, not_83_out, a4, a5, not_84_out);
  and and_44 (and_44_out, a1, a3, not_85_out, a5);
  and and_45 (and_45_out, a1, a3, a5, a6);
  and and_46 (and_46_out, not_86_out, not_87_out, not_88_out, not_89_out, a6);
  and and_47 (and_47_out, not_90_out, not_91_out, not_92_out, a5, a6);
  and and_48 (and_48_out, not_93_out, not_94_out, a4, a5, not_95_out);
  and and_49 (and_49_out, not_96_out, not_97_out, a3, not_98_out, not_99_out, not_100_out);
  and and_50 (and_50_out, not_101_out, not_102_out, a3, a4, not_103_out, a6);
  and and_51 (and_51_out, a2, not_104_out, not_105_out, not_106_out);
  and and_52 (and_52_out, a2, not_107_out, a5, not_108_out);
  and and_53 (and_53_out, a2, not_109_out, a4, a6);
  and and_54 (and_54_out, a2, a4, a5, a6);
  and and_55 (and_55_out, a2, a3, a4, not_110_out, not_111_out);
  and and_56 (and_56_out, a1, not_112_out, a4, not_113_out);
  and and_57 (and_57_out, a1, a4, a5, not_114_out);
  and and_58 (and_58_out, a1, a3, not_115_out, a6);
  or or_3 (A2_2, and_6_out, and_7_out, and_8_out, and_9_out, and_10_out);
  or or_4 (A3_2, and_11_out, and_12_out, and_13_out, and_14_out, and_15_out, and_16_out, and_17_out, and_18_out, and_19_out, and_20_out, and_21_out, and_22_out);
  or or_5 (B0, and_23_out, and_24_out, and_25_out, and_26_out, and_27_out, and_28_out, and_29_out, and_30_out, and_31_out, and_32_out);
  or or_6 (B1, and_33_out, and_34_out, and_35_out, and_36_out, and_37_out, and_38_out, and_39_out, and_40_out, and_41_out, and_42_out, and_43_out, and_44_out, and_45_out);
  or or_7 (B2, and_46_out, and_47_out, and_48_out, and_49_out, and_50_out, and_51_out, and_52_out, and_53_out, and_54_out, and_55_out, and_56_out, and_57_out, and_58_out);

  assign B3 = a7;
endmodule

module _7_segment (
  input  A0,
  input  A1,
  input  A2,
  input  A3,
  output A,
  output B,
  output C,
  output D,
  output E,
  output F,
  output G
);

  wire and_1_out, and_2_out, and_3_out, and_4_out, and_5_out, and_6_out, and_7_out, and_8_out, and_9_out,
       and_10_out, and_11_out, and_12_out, and_13_out, and_14_out, and_15_out, and_16_out, not_1_out,
       not_2_out, not_3_out, not_4_out, not_5_out, not_6_out, not_7_out, not_8_out, not_9_out, not_10_out,
       not_11_out, not_12_out, not_13_out, not_14_out, not_15_out, not_16_out, not_17_out, not_18_out,
       not_19_out, not_20_out, not_21_out;

  not not_1 (not_1_out, A1);
  and and_1 (and_1_out, not_1_out, not_2_out);
  not not_2 (not_2_out, A3);
  and and_2 (and_2_out, A1, A3);
  not not_3 (not_3_out, A1);
  not not_4 (not_4_out, A2);
  and and_3 (and_3_out, not_4_out, not_5_out);
  not not_5 (not_5_out, A3);
  and and_4 (and_4_out, A2, A3);
  not not_6 (not_6_out, A2);
  or or_1 (C, not_6_out, A3, A1);
  not not_7 (not_7_out, A1);
  and and_5 (and_5_out, not_7_out, not_8_out);
  not not_8 (not_8_out, A3);
  not not_9 (not_9_out, A1);
  and and_6 (and_6_out, not_9_out, A2);
  and and_7 (and_7_out, A2, not_10_out);
  not not_10 (not_10_out, A3);
  and and_8 (and_8_out, A1, not_11_out, A3);
  not not_11 (not_11_out, A2);
  not not_12 (not_12_out, A1);
  and and_9 (and_9_out, not_12_out, not_13_out);
  not not_13 (not_13_out, A3);
  and and_10 (and_10_out, A2, not_14_out);
  not not_14 (not_14_out, A3);
  not not_15 (not_15_out, A2);
  and and_11 (and_11_out, not_15_out, not_16_out);
  not not_16 (not_16_out, A3);
  and and_12 (and_12_out, A1, not_17_out);
  not not_17 (not_17_out, A2);
  and and_13 (and_13_out, A1, not_18_out);
  not not_18 (not_18_out, A3);
  not not_19 (not_19_out, A1);
  and and_14 (and_14_out, not_19_out, A2, A3);
  and and_15 (and_15_out, A1, not_20_out);
  not not_20 (not_20_out, A2);
  and and_16 (and_16_out, A1, not_21_out);
  not not_21 (not_21_out, A3);
  or or_2 (A, and_1_out, A2, and_2_out, A0);
  or or_3 (B, not_3_out, and_3_out, and_4_out);
  or or_4 (D, and_5_out, and_6_out, and_7_out, and_8_out, A0);
  or or_5 (E, and_9_out, and_10_out);
  or or_6 (F, and_11_out, and_12_out, and_13_out, A0);
  or or_7 (G, and_14_out, and_15_out, and_16_out, A0);
endmodule
