// Logisim project exp_2_DHRUV.circ as structural Verilog: 1 circuit, main circuit main
module main (
  input  As,
  input  Bs,
  input  M,
  input  [6:0] A,
  input  [6:0] B,
  input  [6:0] in_6,
  output signs,
  output calling,
  output [6:0] Result_A,
  output E,
  output [6:0] Final_A,
  output Final_As,
  output AVF
);

  wire comparator_1_eq, multiplexer_2_out, multiplexer_4_out, not_3_out;
  wire [6:0] adder_2_out, multiplexer_1_out, multiplexer_3_out, not_1_out, not_2_out;

  xor xor_1 (signs, As, Bs);
  assign not_1_out = ~B;  // NOT_Gate not_1, 7 bits wide
  Multiplexer #(.width(7), .enable("false")) multiplexer_1 (
    .in0(B), .in1(not_1_out), .out(multiplexer_1_out), .sel(calling));
  Comparator #(.width(7)) comparator_1 (.a(Result_A), .b(in_6), .eq(comparator_1_eq));  // open: gt, lt
  Adder #(.width(7)) adder_1 (.a(A), .b(multiplexer_1_out), .out(Result_A), .cin(calling), .cout(E));
  xor xor_2 (calling, signs, M);
  Multiplexer #(.enable("false")) multiplexer_2 (.in0(As), .in1(1'b0), .out(multiplexer_2_out), .sel(comparator_1_eq));
  assign not_2_out = ~Result_A;  // NOT_Gate not_2, 7 bits wide
  not not_3 (not_3_out, As);
  Multiplexer #(.width(7), .enable("false")) multiplexer_3 (
    .in0(adder_2_out), .in1(Result_A), .out(multiplexer_3_out), .sel(E));
  Multiplexer #(.enable("false")) multiplexer_4 (
    .in0(not_3_out), .in1(multiplexer_2_out), .out(multiplexer_4_out), .sel(E));
  Adder #(.width(7)) adder_2 (.a(not_2_out), .b(in_6), .out(adder_2_out), .cin(calling));  // open: cout
  Multiplexer #(.width(7), .enable("false")) multiplexer_5 (
    .in0(Result_A), .in1(multiplexer_3_out), .out(Final_A), .sel(calling));
  Multiplexer #(.enable("false")) multiplexer_6 (.in0(As), .in1(multiplexer_4_out), .out(Final_As), .sel(calling));
  Multiplexer #(.enable("false")) multiplexer_7 (.in0(E), .in1(1'b0), .out(AVF), .sel(calling));

  // Notes on the sheet:
  //   Final_As: pull=up
  //   Sign bit of number 1
  //   Sign bit of number 2
  //   Magnitude part of number A
  //   Magnitude part of number B
  //   M=0 : Addition
  //   Signs=0 : Both numbers have same sign.
  //   Signs=1 : Both numbers have different sign.
  //   M=1 : Subtraction
  //   Function 1 tasks: Add magnitudes of both numbers and use sign of number A
  //   Function 2 tasks: Substract smaller magnitude from larger magnitude and use sign of larger magnitude number.
  //   calling=0 : Call Function 1
  //   calling=1 : Call Function 2
  //   23CS041
endmodule
