// Logisim project exp_3_2_DHRUV.circ as structural Verilog: 1 circuit, main circuit main
module main (
  input  [1:0] Select,
  input  [3:0] Input_for_register_D,
  input  [3:0] Input_for_register_C,
  input  [3:0] Input_for_register_B,
  input  [3:0] Input_for_register_A,
  input  CLR,
  output [3:0] Coman_Bus,
  output [3:0] out_8,
  output [3:0] out_9,
  output [3:0] out_10,
  output [3:0] out_11
);

  wire clock_1_out, decoder_1_out0, decoder_1_out1, decoder_1_out2, decoder_1_out3;

  Clock clock_1 (.out(clock_1_out));
  Decoder #(.select(2)) decoder_1 (
    .out0(decoder_1_out0), .out1(decoder_1_out1), .out2(decoder_1_out2), .out3(decoder_1_out3), .sel(Select));  // open: en
  Register #(.width(4)) RegisterD (.D(Input_for_register_D), .en(1'b1), .Q(out_8), .clk(clock_1_out), .clr(CLR));
  assign Coman_Bus[3] = decoder_1_out0 ? out_11[3] : 1'bz;  // Controlled_Buffer controlled_buffer_1
  assign Coman_Bus[3] = decoder_1_out1 ? out_10[3] : 1'bz;  // Controlled_Buffer controlled_buffer_2
  assign Coman_Bus[3] = decoder_1_out2 ? out_9[3] : 1'bz;  // Controlled_Buffer controlled_buffer_3
  assign Coman_Bus[3] = decoder_1_out3 ? out_8[3] : 1'bz;  // Controlled_Buffer controlled_buffer_4
  assign Coman_Bus[2] = decoder_1_out0 ? out_11[2] : 1'bz;  // Controlled_Buffer controlled_buffer_5
  assign Coman_Bus[2] = decoder_1_out1 ? out_10[2] : 1'bz;  // Controlled_Buffer controlled_buffer_6
  assign Coman_Bus[2] = decoder_1_out2 ? out_9[2] : 1'bz;  // Controlled_Buffer controlled_buffer_7
  assign Coman_Bus[2] = decoder_1_out3 ? out_8[2] : 1'bz;  // Controlled_Buffer controlled_buffer_8
  Register #(.width(4)) Register_C (.D(Input_for_register_C), .en(1'b1), .Q(out_9), .clk(clock_1_out), .clr(CLR));
  assign Coman_Bus[1] = decoder_1_out0 ? out_11[1] : 1'bz;  // Controlled_Buffer controlled_buffer_9
  assign Coman_Bus[1] = decoder_1_out1 ? out_10[1] : 1'bz;  // Controlled_Buffer controlled_buffer_10
  assign Coman_Bus[1] = decoder_1_out2 ? out_9[1] : 1'bz;  // Controlled_Buffer controlled_buffer_11
  assign Coman_Bus[1] = decoder_1_out3 ? out_8[1] : 1'bz;  // Controlled_Buffer controlled_buffer_12
  Register #(.width(4)) Register_B (.D(Input_for_register_B), .en(1'b1), .Q(out_10), .clk(clock_1_out), .clr(CLR));
  assign Coman_Bus[0] = decoder_1_out0 ? out_11[0] : 1'bz;  // Controlled_Buffer controlled_buffer_13
  assign Coman_Bus[0] = decoder_1_out1 ? out_10[0] : 1'bz;  // Controlled_Buffer controlled_buffer_14
  assign Coman_Bus[0] = decoder_1_out2 ? out_9[0] : 1'bz;  // Controlled_Buffer controlled_buffer_15
  assign Coman_Bus[0] = decoder_1_out3 ? out_8[0] : 1'bz;  // Controlled_Buffer controlled_buffer_16
  Register #(.width(4)) Register_A (.D(Input_for_register_A), .en(1'b1), .Q(out_11), .clk(clock_1_out), .clr(CLR));

  // Notes on the sheet:
  //   Select 00 : A
  //   Select 01 : B
  //   Select 10 : C
  //   Select 11 : D
  //   Register A
  //   A3
  //   B3
  //   C3
  //   D3
  //   A2
  //   B2
  //   C2
  //   D2
  //   A1
  //   B1
  //   C1
  //   D1
  //   A0
  //   B0
  //   C0
  //   D0
  //   23CS041
endmodule
