// Logisim project exp_3_DHRUV.circ as structural Verilog: 1 circuit, main circuit main
module main (
  input  [1:0] Select,
  input  [3:0] Input_for_register_D,
  input  [3:0] Input_for_register_C,
  input  [3:0] Input_for_register_B,
  input  [3:0] Input_for_register_A,
  input  CLR,
  output [3:0] Coman_Bus,
  output [3:0] out_8,
  output [3:0] out_9,
  output [3:0] out_10,
  output [3:0] out_11
);

  wire clock_1_out;

  Clock clock_1 (.out(clock_1_out));
  Multiplexer #(.select(2), .enable("false")) multiplexer_1 (
    .in0(out_11[3]), .in1(out_10[3]), .in2(out_9[3]), .in3(out_8[3]), .out(Coman_Bus[3]), .sel(Select));
  Register #(.width(4)) RegisterD (.D(Input_for_register_D), .en(1'b1), .Q(out_8), .clk(clock_1_out), .clr(CLR));
  Multiplexer #(.select(2), .enable("false")) multiplexer_2 (
    .in0(out_11[2]), .in1(out_10[2]), .in2(out_9[2]), .in3(out_8[2]), .out(Coman_Bus[2]), .sel(Select));
  Register #(.width(4)) Register_C (.D(Input_for_register_C), .en(1'b1), .Q(out_9), .clk(clock_1_out), .clr(CLR));
  Register #(.width(4)) Register_B (.D(Input_for_register_B), .en(1'b1), .Q(out_10), .clk(clock_1_out), .clr(CLR));
  Multiplexer #(.select(2), .enable("false")) multiplexer_3 (
    .in0(out_11[1]), .in1(out_10[1]), .in2(out_9[1]), .in3(out_8[1]), .out(Coman_Bus[1]), .sel(Select));
  Register #(.width(4)) Register_A (.D(Input_for_register_A), .en(1'b1), .Q(out_11), .clk(clock_1_out), .clr(CLR));
  Multiplexer #(.select(2), .enable("false")) multiplexer_4 (
    .in0(out_11[0]), .in1(out_10[0]), .in2(out_9[0]), .in3(out_8[0]), .out(Coman_Bus[0]), .sel(Select));

  // Notes on the sheet:
  //   Select 00 : A
  //   Select 01 : B
  //   Select 10 : C
  //   Select 11 : D
  //   23CS041
  //   Bit 3
  //   Bit 2
  //   Bit 1
  //   Bit 0
endmodule
