// Logisim project exp_4_DHRUV.circ as structural Verilog: 17 circuits, main circuit 4_bit_arithmetic
module _1_bit_arithmetic (
  input  Cin,
  input  A0,
  input  B0,
  input  [1:0] S1S0,
  output S0,
  output Cout
);

  wire multiplexer_1_out, not_1_out, not_2_out, xor_1_out;

  not not_1 (not_1_out, B0);
  xor xor_1 (xor_1_out, B0, B0);
  not not_2 (not_2_out, xor_1_out);
  Multiplexer #(.select(2), .enable("false")) multiplexer_1 (
    .in0(B0), .in1(not_1_out), .in2(xor_1_out), .in3(not_2_out), .out(multiplexer_1_out), .sel(S1S0));
  Adder #(.width(1)) adder_1 (.a(A0), .b(multiplexer_1_out), .out(S0), .cin(Cin), .cout(Cout));

  // Notes on the sheet:
  //   23CS041
endmodule

module _2_bit_arithmetic (
  input  Cin,
  input  [1:0] A1A0,
  input  [1:0] B1B0,
  input  [1:0] S1S0,
  output [1:0] S1S0_2,
  output Cout
);

  wire adder_1_cout, multiplexer_1_out, multiplexer_2_out, not_1_out, not_2_out, not_3_out, not_4_out,
       xor_1_out, xor_2_out;

  not not_1 (not_1_out, B1B0[0]);
  not not_2 (not_2_out, xor_1_out);
  xor xor_1 (xor_1_out, B1B0[0], B1B0[0]);
  not not_3 (not_3_out, B1B0[1]);
  not not_4 (not_4_out, xor_2_out);
  xor xor_2 (xor_2_out, B1B0[1], B1B0[1]);
  Multiplexer #(.select(2), .enable("false")) multiplexer_1 (
    .in0(B1B0[0]), .in1(not_1_out), .in2(xor_1_out), .in3(not_2_out), .out(multiplexer_1_out), .sel(S1S0));
  Multiplexer #(.select(2), .enable("false")) multiplexer_2 (
    .in0(B1B0[1]), .in1(not_3_out), .in2(xor_2_out), .in3(not_4_out), .out(multiplexer_2_out), .sel(S1S0));
  Adder #(.width(1)) adder_1 (.a(A1A0[0]), .b(multiplexer_1_out), .out(S1S0_2[0]), .cin(Cin), .cout(adder_1_cout));
  Adder #(.width(1)) adder_2 (.a(A1A0[1]), .b(multiplexer_2_out), .out(S1S0_2[1]), .cin(adder_1_cout), .cout(Cout));

  // Notes on the sheet:
  //   23CS041
endmodule

module _4_bit_arithmetic (
  input  [1:0] S1S0,
  input  Cin,
  input  [3:0] A3A2A1A0,
  input  [3:0] B3B2B1B0,
  output [3:0] S3S2S1S0,
  output Cout
);

  wire adder_1_cout, adder_2_cout, adder_3_cout, multiplexer_1_out, multiplexer_2_out, multiplexer_3_out,
       multiplexer_4_out, not_1_out, not_2_out, not_3_out, not_4_out, not_5_out, not_6_out, not_7_out,
       not_8_out, xor_1_out, xor_2_out, xor_3_out, xor_4_out;

  not not_1 (not_1_out, B3B2B1B0[0]);
  xor xor_1 (xor_1_out, B3B2B1B0[0], B3B2B1B0[0]);
  not not_2 (not_2_out, xor_1_out);
  not not_3 (not_3_out, B3B2B1B0[1]);
  not not_4 (not_4_out, xor_2_out);
  xor xor_2 (xor_2_out, B3B2B1B0[1], B3B2B1B0[1]);
  not not_5 (not_5_out, B3B2B1B0[2]);
  not not_6 (not_6_out, xor_3_out);
  xor xor_3 (xor_3_out, B3B2B1B0[2], B3B2B1B0[2]);
  not not_7 (not_7_out, B3B2B1B0[3]);
  xor xor_4 (xor_4_out, B3B2B1B0[3], B3B2B1B0[3]);
  Multiplexer #(.select(2), .enable("false")) multiplexer_1 (
    .in0(B3B2B1B0[0]), .in1(not_1_out), .in2(xor_1_out), .in3(not_2_out), .out(multiplexer_1_out), .sel(S1S0));
  Multiplexer #(.select(2), .enable("false")) multiplexer_2 (
    .in0(B3B2B1B0[1]), .in1(not_3_out), .in2(xor_2_out), .in3(not_4_out), .out(multiplexer_2_out), .sel(S1S0));
  Multiplexer #(.select(2), .enable("false")) multiplexer_3 (
    .in0(B3B2B1B0[2]), .in1(not_5_out), .in2(xor_3_out), .in3(not_6_out), .out(multiplexer_3_out), .sel(S1S0));
  Multiplexer #(.select(2), .enable("false")) multiplexer_4 (
    .in0(B3B2B1B0[3]), .in1(not_7_out), .in2(xor_4_out), .in3(not_8_out), .out(multiplexer_4_out), .sel(S1S0));
  not not_8 (not_8_out, xor_4_out);
  Adder #(.width(1)) adder_1 (
    .a(A3A2A1A0[0]), .b(multiplexer_1_out), .out(S3S2S1S0[0]), .cin(Cin), .cout(adder_1_cout));
  Adder #(.width(1)) adder_2 (
    .a(A3A2A1A0[1]), .b(multiplexer_2_out), .out(S3S2S1S0[1]), .cin(adder_1_cout), .cout(adder_2_cout));
  Adder #(.width(1)) adder_3 (
    .a(A3A2A1A0[2]), .b(multiplexer_3_out), .out(S3S2S1S0[2]), .cin(adder_2_cout), .cout(adder_3_cout));
  Adder #(.width(1)) adder_4 (
    .a(A3A2A1A0[3]), .b(multiplexer_4_out), .out(S3S2S1S0[3]), .cin(adder_3_cout), .cout(Cout));

  // Notes on the sheet:
  //   23CS041
endmodule

module _8_bit_arithmetic (
  input  Cin,
  input  [7:0] A7A6A5A4A3A2A1A0,
  input  [7:0] B7B6B5B4B3B2B1B0,
  input  [1:0] S1S0,
  output [7:0] S3S2S1S0,
  output Cout
);

  wire adder_1_cout, adder_2_cout, adder_3_cout, adder_5_cout, adder_6_cout, adder_7_cout, multiplexer_1_out,
       multiplexer_2_out, multiplexer_3_out, multiplexer_4_out, multiplexer_5_out, multiplexer_6_out,
       multiplexer_7_out, multiplexer_8_out, not_1_out, not_2_out, not_3_out, not_4_out, not_5_out,
       not_6_out, not_7_out, not_8_out, not_9_out, not_10_out, not_11_out, not_12_out, not_13_out,
       not_14_out, not_15_out, not_16_out, xor_1_out, xor_2_out, xor_3_out, xor_4_out, xor_5_out, xor_6_out,
       xor_7_out, xor_8_out;

  not not_1 (not_1_out, B7B6B5B4B3B2B1B0[0]);
  xor xor_1 (xor_1_out, B7B6B5B4B3B2B1B0[0], B7B6B5B4B3B2B1B0[0]);
  not not_2 (not_2_out, xor_1_out);
  not not_3 (not_3_out, B7B6B5B4B3B2B1B0[1]);
  not not_4 (not_4_out, xor_2_out);
  xor xor_2 (xor_2_out, B7B6B5B4B3B2B1B0[1], B7B6B5B4B3B2B1B0[1]);
  not not_5 (not_5_out, B7B6B5B4B3B2B1B0[2]);
  not not_6 (not_6_out, xor_3_out);
  xor xor_3 (xor_3_out, B7B6B5B4B3B2B1B0[2], B7B6B5B4B3B2B1B0[2]);
  not not_7 (not_7_out, B7B6B5B4B3B2B1B0[3]);
  xor xor_4 (xor_4_out, B7B6B5B4B3B2B1B0[3], B7B6B5B4B3B2B1B0[3]);
  not not_8 (not_8_out, B7B6B5B4B3B2B1B0[4]);
  not not_9 (not_9_out, xor_5_out);
  xor xor_5 (xor_5_out, B7B6B5B4B3B2B1B0[4], B7B6B5B4B3B2B1B0[4]);
  not not_10 (not_10_out, B7B6B5B4B3B2B1B0[5]);
  xor xor_6 (xor_6_out, B7B6B5B4B3B2B1B0[5], B7B6B5B4B3B2B1B0[5]);
  not not_11 (not_11_out, xor_6_out);
  not not_12 (not_12_out, B7B6B5B4B3B2B1B0[6]);
  not not_13 (not_13_out, xor_7_out);
  xor xor_7 (xor_7_out, B7B6B5B4B3B2B1B0[6], B7B6B5B4B3B2B1B0[6]);
  not not_14 (not_14_out, B7B6B5B4B3B2B1B0[7]);
  xor xor_8 (xor_8_out, B7B6B5B4B3B2B1B0[7], B7B6B5B4B3B2B1B0[7]);
  Multiplexer #(.select(2), .enable("false")) multiplexer_1 (
    .in0(B7B6B5B4B3B2B1B0[0]), .in1(not_1_out), .in2(xor_1_out), .in3(not_2_out), .out(multiplexer_1_out),
    .sel(S1S0));
  Multiplexer #(.select(2), .enable("false")) multiplexer_2 (
    .in0(B7B6B5B4B3B2B1B0[1]), .in1(not_3_out), .in2(xor_2_out), .in3(not_4_out), .out(multiplexer_2_out),
    .sel(S1S0));
  Multiplexer #(.select(2), .enable("false")) multiplexer_3 (
    .in0(B7B6B5B4B3B2B1B0[2]), .in1(not_5_out), .in2(xor_3_out), .in3(not_6_out), .out(multiplexer_3_out),
    .sel(S1S0));
  Multiplexer #(.select(2), .enable("false")) multiplexer_4 (
    .in0(B7B6B5B4B3B2B1B0[3]), .in1(not_7_out), .in2(xor_4_out), .in3(not_15_out), .out(multiplexer_4_out),
    .sel(S1S0));
  not not_15 (not_15_out, xor_4_out);
  Multiplexer #(.select(2), .enable("false")) multiplexer_5 (
    .in0(B7B6B5B4B3B2B1B0[4]), .in1(not_8_out), .in2(xor_5_out), .in3(not_9_out), .out(multiplexer_5_out),
    .sel(S1S0));
  Multiplexer #(.select(2), .enable("false")) multiplexer_6 (
    .in0(B7B6B5B4B3B2B1B0[5]), .in1(not_10_out), .in2(xor_6_out), .in3(not_11_out), .out(multiplexer_6_out),
    .sel(S1S0));
  Multiplexer #(.select(2), .enable("false")) multiplexer_7 (
    .in0(B7B6B5B4B3B2B1B0[6]), .in1(not_12_out), .in2(xor_7_out), .in3(not_13_out), .out(multiplexer_7_out),
    .sel(S1S0));
  Multiplexer #(.select(2), .enable("false")) multiplexer_8 (
    .in0(B7B6B5B4B3B2B1B0[7]), .in1(not_14_out), .in2(xor_8_out), .in3(not_16_out), .out(multiplexer_8_out),
    .sel(S1S0));
  not not_16 (not_16_out, xor_8_out);
  Adder #(.width(1)) adder_1 (
    .a(A7A6A5A4A3A2A1A0[0]), .b(multiplexer_1_out), .out(S3S2S1S0[0]), .cin(Cin), .cout(adder_1_cout));
  Adder #(.width(1)) adder_2 (
    .a(A7A6A5A4A3A2A1A0[1]), .b(multiplexer_2_out), .out(S3S2S1S0[1]), .cin(adder_1_cout), .cout(adder_2_cout));
  Adder #(.width(1)) adder_3 (
    .a(A7A6A5A4A3A2A1A0[2]), .b(multiplexer_3_out), .out(S3S2S1S0[2]), .cin(adder_2_cout), .cout(adder_3_cout));
  Adder #(.width(1)) adder_4 (
    .a(A7A6A5A4A3A2A1A0[3]), .b(multiplexer_4_out), .out(S3S2S1S0[3]), .cin(adder_3_cout));  // open: cout
  Adder #(.width(1)) adder_5 (
    .a(A7A6A5A4A3A2A1A0[4]), .b(multiplexer_5_out), .out(S3S2S1S0[4]), .cout(adder_5_cout));  // open: cin
  Adder #(.width(1)) adder_6 (
    .a(A7A6A5A4A3A2A1A0[5]), .b(multiplexer_6_out), .out(S3S2S1S0[5]), .cin(adder_5_cout), .cout(adder_6_cout));
  Adder #(.width(1)) adder_7 (
    .a(A7A6A5A4A3A2A1A0[6]), .b(multiplexer_7_out), .out(S3S2S1S0[6]), .cin(adder_6_cout), .cout(adder_7_cout));
  Adder #(.width(1)) adder_8 (
    .a(A7A6A5A4A3A2A1A0[7]), .b(multiplexer_8_out), .out(S3S2S1S0[7]), .cin(adder_7_cout), .cout(Cout));

  // Notes on the sheet:
  //   23CS041
endmodule

module _1_bit_logical (
  input  B0,
  input  A0,
  input  [1:0] S1S0,
  output E0
);

  wire and_1_out, not_1_out, or_1_out, xor_1_out;

  and and_1 (and_1_out, A0, B0);
  or or_1 (or_1_out, A0, B0);
  not not_1 (not_1_out, A0);
  xor xor_1 (xor_1_out, A0, B0);
  Multiplexer #(.select(2), .enable("false")) multiplexer_1 (
    .in0(and_1_out), .in1(or_1_out), .in2(xor_1_out), .in3(not_1_out), .out(E0), .sel(S1S0));

  // Notes on the sheet:
  //   23CS041
endmodule

module _2_bit_logical (
  input  [1:0] A1A0,
  input  [1:0] B1B0,
  input  [1:0] S1S0,
  output [1:0] Output
);

  wire and_1_out, and_2_out, not_1_out, not_2_out, or_1_out, or_2_out, xor_1_out, xor_2_out;

  and and_1 (and_1_out, A1A0[0], B1B0[0]);
  or or_1 (or_1_out, A1A0[0], B1B0[0]);
  xor xor_1 (xor_1_out, A1A0[0], B1B0[0]);
  not not_1 (not_1_out, A1A0[0]);
  and and_2 (and_2_out, A1A0[1], B1B0[1]);
  or or_2 (or_2_out, A1A0[1], B1B0[1]);
  xor xor_2 (xor_2_out, A1A0[1], B1B0[1]);
  not not_2 (not_2_out, A1A0[1]);
  Multiplexer #(.select(2), .enable("false")) multiplexer_1 (
    .in0(and_1_out), .in1(or_1_out), .in2(xor_1_out), .in3(not_1_out), .out(Output[0]), .sel(S1S0));
  Multiplexer #(.select(2), .enable("false")) multiplexer_2 (
    .in0(and_2_out), .in1(or_2_out), .in2(xor_2_out), .in3(not_2_out), .out(Output[1]), .sel(S1S0));

  // Notes on the sheet:
  //   23CS041
endmodule

module _4_bit_logical (
  input  [3:0] A3A2A1A0,
  input  [3:0] B3B2B1B0,
  input  [1:0] S1S0,
  output [3:0] S3S2S1S0
);

  wire and_1_out, and_2_out, and_3_out, and_4_out, not_1_out, not_2_out, not_3_out, not_4_out, or_1_out,
       or_2_out, or_3_out, or_4_out, xor_1_out, xor_2_out, xor_3_out, xor_4_out;

  and and_1 (and_1_out, A3A2A1A0[0], B3B2B1B0[0]);
  or or_1 (or_1_out, A3A2A1A0[0], B3B2B1B0[0]);
  xor xor_1 (xor_1_out, A3A2A1A0[0], B3B2B1B0[0]);
  not not_1 (not_1_out, A3A2A1A0[0]);
  and and_2 (and_2_out, A3A2A1A0[1], B3B2B1B0[1]);
  or or_2 (or_2_out, A3A2A1A0[1], B3B2B1B0[1]);
  xor xor_2 (xor_2_out, A3A2A1A0[1], B3B2B1B0[1]);
  not not_2 (not_2_out, A3A2A1A0[1]);
  and and_3 (and_3_out, A3A2A1A0[2], B3B2B1B0[2]);
  or or_3 (or_3_out, A3A2A1A0[2], B3B2B1B0[2]);
  xor xor_3 (xor_3_out, A3A2A1A0[2], B3B2B1B0[2]);
  not not_3 (not_3_out, A3A2A1A0[2]);
  and and_4 (and_4_out, A3A2A1A0[3], B3B2B1B0[3]);
  or or_4 (or_4_out, A3A2A1A0[3], B3B2B1B0[3]);
  xor xor_4 (xor_4_out, A3A2A1A0[3], B3B2B1B0[3]);
  not not_4 (not_4_out, A3A2A1A0[3]);
  Multiplexer #(.select(2), .enable("false")) multiplexer_1 (
    .in0(and_1_out), .in1(or_1_out), .in2(xor_1_out), .in3(not_1_out), .out(S3S2S1S0[0]), .sel(S1S0));
  Multiplexer #(.select(2), .enable("false")) multiplexer_2 (
    .in0(and_2_out), .in1(or_2_out), .in2(xor_2_out), .in3(not_2_out), .out(S3S2S1S0[1]), .sel(S1S0));
  Multiplexer #(.select(2), .enable("false")) multiplexer_3 (
    .in0(and_3_out), .in1(or_3_out), .in2(xor_3_out), .in3(not_3_out), .out(S3S2S1S0[2]), .sel(S1S0));
  Multiplexer #(.select(2), .enable("false")) multiplexer_4 (
    .in0(and_4_out), .in1(or_4_out), .in2(xor_4_out), .in3(not_4_out), .out(S3S2S1S0[3]), .sel(S1S0));

  // Notes on the sheet:
  //   23CS041
endmodule

module _8_bit_logical (
  input  [7:0] A7A6A5A4A3A2A1A0,
  input  [1:0] S1S0,
  input  [7:0] B7B6B5B4B3B2B1B0,
  output [7:0] S7S6S5S4S3S2S1S0
);

  wire and_1_out, and_2_out, and_3_out, and_4_out, and_5_out, and_6_out, and_7_out, and_8_out, not_1_out,
       not_2_out, not_3_out, not_4_out, not_5_out, not_6_out, not_7_out, not_8_out, or_1_out, or_2_out,
       or_3_out, or_4_out, or_5_out, or_6_out, or_7_out, or_8_out, xor_1_out, xor_2_out, xor_3_out,
       xor_4_out, xor_5_out, xor_6_out, xor_7_out, xor_8_out;

  and and_1 (and_1_out, A7A6A5A4A3A2A1A0[0], B7B6B5B4B3B2B1B0[0]);
  or or_1 (or_1_out, A7A6A5A4A3A2A1A0[0], B7B6B5B4B3B2B1B0[0]);
  xor xor_1 (xor_1_out, A7A6A5A4A3A2A1A0[0], B7B6B5B4B3B2B1B0[0]);
  not not_1 (not_1_out, A7A6A5A4A3A2A1A0[0]);
  and and_2 (and_2_out, A7A6A5A4A3A2A1A0[1], B7B6B5B4B3B2B1B0[1]);
  or or_2 (or_2_out, A7A6A5A4A3A2A1A0[1], B7B6B5B4B3B2B1B0[1]);
  xor xor_2 (xor_2_out, A7A6A5A4A3A2A1A0[1], B7B6B5B4B3B2B1B0[1]);
  not not_2 (not_2_out, A7A6A5A4A3A2A1A0[1]);
  and and_3 (and_3_out, A7A6A5A4A3A2A1A0[2], B7B6B5B4B3B2B1B0[2]);
  or or_3 (or_3_out, A7A6A5A4A3A2A1A0[2], B7B6B5B4B3B2B1B0[2]);
  xor xor_3 (xor_3_out, A7A6A5A4A3A2A1A0[2], B7B6B5B4B3B2B1B0[2]);
  not not_3 (not_3_out, A7A6A5A4A3A2A1A0[2]);
  and and_4 (and_4_out, A7A6A5A4A3A2A1A0[3], B7B6B5B4B3B2B1B0[3]);
  or or_4 (or_4_out, A7A6A5A4A3A2A1A0[3], B7B6B5B4B3B2B1B0[3]);
  xor xor_4 (xor_4_out, A7A6A5A4A3A2A1A0[3], B7B6B5B4B3B2B1B0[3]);
  not not_4 (not_4_out, A7A6A5A4A3A2A1A0[3]);
  and and_5 (and_5_out, A7A6A5A4A3A2A1A0[4], B7B6B5B4B3B2B1B0[4]);
  or or_5 (or_5_out, A7A6A5A4A3A2A1A0[4], B7B6B5B4B3B2B1B0[4]);
  xor xor_5 (xor_5_out, A7A6A5A4A3A2A1A0[4], B7B6B5B4B3B2B1B0[4]);
  not not_5 (not_5_out, A7A6A5A4A3A2A1A0[4]);
  and and_6 (and_6_out, A7A6A5A4A3A2A1A0[5], B7B6B5B4B3B2B1B0[5]);
  or or_6 (or_6_out, A7A6A5A4A3A2A1A0[5], B7B6B5B4B3B2B1B0[5]);
  xor xor_6 (xor_6_out, A7A6A5A4A3A2A1A0[5], B7B6B5B4B3B2B1B0[5]);
  not not_6 (not_6_out, A7A6A5A4A3A2A1A0[5]);
  and and_7 (and_7_out, A7A6A5A4A3A2A1A0[6], B7B6B5B4B3B2B1B0[6]);
  or or_7 (or_7_out, A7A6A5A4A3A2A1A0[6], B7B6B5B4B3B2B1B0[6]);
  xor xor_7 (xor_7_out, A7A6A5A4A3A2A1A0[6], B7B6B5B4B3B2B1B0[6]);
  not not_7 (not_7_out, A7A6A5A4A3A2A1A0[6]);
  and and_8 (and_8_out, A7A6A5A4A3A2A1A0[7], B7B6B5B4B3B2B1B0[7]);
  or or_8 (or_8_out, A7A6A5A4A3A2A1A0[7], B7B6B5B4B3B2B1B0[7]);
  xor xor_8 (xor_8_out, A7A6A5A4A3A2A1A0[7], B7B6B5B4B3B2B1B0[7]);
  not not_8 (not_8_out, A7A6A5A4A3A2A1A0[7]);
  Multiplexer #(.select(2), .enable("false")) multiplexer_1 (
    .in0(and_1_out), .in1(or_1_out), .in2(xor_1_out), .in3(not_1_out), .out(S7S6S5S4S3S2S1S0[0]), .sel(S1S0));
  Multiplexer #(.select(2), .enable("false")) multiplexer_2 (
    .in0(and_2_out), .in1(or_2_out), .in2(xor_2_out), .in3(not_2_out), .out(S7S6S5S4S3S2S1S0[1]), .sel(S1S0));
  Multiplexer #(.select(2), .enable("false")) multiplexer_3 (
    .in0(and_3_out), .in1(or_3_out), .in2(xor_3_out), .in3(not_3_out), .out(S7S6S5S4S3S2S1S0[2]), .sel(S1S0));
  Multiplexer #(.select(2), .enable("false")) multiplexer_4 (
    .in0(and_4_out), .in1(or_4_out), .in2(xor_4_out), .in3(not_4_out), .out(S7S6S5S4S3S2S1S0[3]), .sel(S1S0));
  Multiplexer #(.select(2), .enable("false")) multiplexer_5 (
    .in0(and_5_out), .in1(or_5_out), .in2(xor_5_out), .in3(not_5_out), .out(S7S6S5S4S3S2S1S0[4]), .sel(S1S0));
  Multiplexer #(.select(2), .enable("false")) multiplexer_6 (
    .in0(and_6_out), .in1(or_6_out), .in2(xor_6_out), .in3(not_6_out), .out(S7S6S5S4S3S2S1S0[5]), .sel(S1S0));
  Multiplexer #(.select(2), .enable("false")) multiplexer_7 (
    .in0(and_7_out), .in1(or_7_out), .in2(xor_7_out), .in3(not_7_out), .out(S7S6S5S4S3S2S1S0[6]), .sel(S1S0));
  Multiplexer #(.select(2), .enable("false")) multiplexer_8 (
    .in0(and_8_out), .in1(or_8_out), .in2(xor_8_out), .in3(not_8_out), .out(S7S6S5S4S3S2S1S0[7]), .sel(S1S0));

  // Notes on the sheet:
  //   23CS041
endmodule

module _1_bit_16logical_functions (
  input  A0,
  input  [3:0] S4S3S1S0,
  input  B0,
  output out_4
);

  wire and_1_out, and_2_out, and_3_out, nand_1_out, nor_1_out, not_1_out, not_2_out, or_1_out, or_2_out,
       or_3_out, xnor_1_out, xor_1_out;

  not not_1 (not_1_out, A0);
  not not_2 (not_2_out, B0);
  xnor xnor_1 (xnor_1_out, A0, B0);
  and and_1 (and_1_out, A0, B0);
  xor xor_1 (xor_1_out, A0, B0);
  or or_1 (or_1_out, A0, B0);
  or or_2 (or_2_out, not_1_out, B0);
  and and_2 (and_2_out, A0, not_2_out);
  and and_3 (and_3_out, not_1_out, B0);
  nor nor_1 (nor_1_out, A0, B0);
  nand nand_1 (nand_1_out, A0, B0);
  or or_3 (or_3_out, A0, not_2_out);
  Multiplexer #(.select(4), .enable("false")) multiplexer_1 (
    .in0(1'b0), .in1(and_1_out), .in2(and_2_out), .in3(A0), .in4(and_3_out), .in5(B0), .in6(xor_1_out),
    .in7(or_1_out), .in8(nor_1_out), .in9(xnor_1_out), .in10(not_2_out), .in11(or_3_out), .in12(not_1_out),
    .in13(or_2_out), .in14(nand_1_out), .in15(1'b1), .out(out_4), .sel(S4S3S1S0));

  // Notes on the sheet:
  //   23CS041
endmodule

module _2_bit_16logical_functions (
  input  [1:0] A1A0,
  input  [1:0] B1B0,
  input  [3:0] S4S3S1S0,
  output out_4,
  output out_5
);

  wire and_1_out, and_2_out, and_3_out, and_4_out, and_5_out, and_6_out, nand_1_out, nand_2_out, nor_1_out,
       nor_2_out, not_1_out, not_2_out, not_3_out, not_4_out, or_1_out, or_2_out, or_3_out, or_4_out,
       or_5_out, or_6_out, xnor_1_out, xnor_2_out, xor_1_out, xor_2_out;

  not not_1 (not_1_out, A1A0[0]);
  not not_2 (not_2_out, A1A0[1]);
  not not_3 (not_3_out, B1B0[0]);
  not not_4 (not_4_out, B1B0[1]);
  and and_1 (and_1_out, A1A0[0], B1B0[0]);
  xor xor_1 (xor_1_out, A1A0[0], B1B0[0]);
  xnor xnor_1 (xnor_1_out, A1A0[0], B1B0[0]);
  or or_1 (or_1_out, not_1_out, B1B0[0]);
  and and_2 (and_2_out, A1A0[1], B1B0[1]);
  xor xor_2 (xor_2_out, A1A0[1], B1B0[1]);
  xnor xnor_2 (xnor_2_out, A1A0[1], B1B0[1]);
  or or_2 (or_2_out, not_2_out, B1B0[1]);
  and and_3 (and_3_out, A1A0[0], not_3_out);
  or or_3 (or_3_out, A1A0[0], B1B0[0]);
  nor nor_1 (nor_1_out, A1A0[0], B1B0[0]);
  and and_4 (and_4_out, A1A0[1], not_4_out);
  or or_4 (or_4_out, A1A0[1], B1B0[1]);
  nor nor_2 (nor_2_out, A1A0[1], B1B0[1]);
  and and_5 (and_5_out, not_1_out, B1B0[0]);
  or or_5 (or_5_out, A1A0[0], not_3_out);
  nand nand_1 (nand_1_out, A1A0[0], B1B0[0]);
  and and_6 (and_6_out, not_2_out, B1B0[1]);
  or or_6 (or_6_out, A1A0[1], not_4_out);
  nand nand_2 (nand_2_out, A1A0[1], B1B0[1]);
  Multiplexer #(.select(4), .enable("false")) multiplexer_1 (
    .in0(1'b0), .in1(and_1_out), .in2(and_3_out), .in3(A1A0[0]), .in4(and_5_out), .in5(B1B0[0]),
    .in6(xor_1_out), .in7(or_3_out), .in8(nor_1_out), .in9(xnor_1_out), .in10(not_3_out), .in11(or_5_out),
    .in12(not_1_out), .in13(or_1_out), .in14(nand_1_out), .in15(1'b1), .out(out_4), .sel(S4S3S1S0));
  Multiplexer #(.select(4), .enable("false")) multiplexer_2 (
    .in0(1'b0), .in1(and_2_out), .in2(and_4_out), .in3(A1A0[1]), .in4(and_6_out), .in5(B1B0[1]),
    .in6(xor_2_out), .in7(or_4_out), .in8(nor_2_out), .in9(xnor_2_out), .in10(not_4_out), .in11(or_6_out),
    .in12(not_2_out), .in13(or_2_out), .in14(nand_2_out), .in15(1'b1), .out(out_5), .sel(S4S3S1S0));

  // Notes on the sheet:
  //   23CS041
endmodule

module _2_bit_bidirectional_shifter (
  input  [1:0] Input,
  input  SHR,
  input  SHL,
  input  Select,
  output [1:0] Output
);

  Multiplexer #(.enable("false")) multiplexer_1 (.in0(SHR), .in1(Input[0]), .out(Output[1]), .sel(Select));
  Multiplexer #(.enable("false")) multiplexer_2 (.in0(Input[1]), .in1(SHL), .out(Output[0]), .sel(Select));

  // Notes on the sheet:
  //   Select 0 : Right shift
  //   Select 1 : Left shift
  //   23CS041
endmodule

module _4_bit_bidirectional_shifter (
  input  [3:0] Input,
  input  SHR,
  input  SHL,
  input  Select,
  output [3:0] Output
);

  Multiplexer #(.enable("false")) multiplexer_1 (.in0(SHR), .in1(Input[2]), .out(Output[3]), .sel(Select));
  Multiplexer #(.enable("false")) multiplexer_2 (.in0(Input[3]), .in1(Input[1]), .out(Output[2]), .sel(Select));
  Multiplexer #(.enable("false")) multiplexer_3 (.in0(Input[2]), .in1(Input[0]), .out(Output[1]), .sel(Select));
  Multiplexer #(.enable("false")) multiplexer_4 (.in0(Input[1]), .in1(SHL), .out(Output[0]), .sel(Select));

  // Notes on the sheet:
  //   Select 1 : Left shift
  //   Select 0 : Right shift
  //   23CS041
endmodule

module _8_bit_bidirectional_shifter (
  input  [7:0] Input,
  input  SHR,
  input  SHL,
  input  Select,
  output [7:0] Output
);

  Multiplexer #(.enable("false")) multiplexer_1 (.in0(SHR), .in1(Input[6]), .out(Output[7]), .sel(Select));
  Multiplexer #(.enable("false")) multiplexer_2 (.in0(Input[7]), .in1(Input[5]), .out(Output[6]), .sel(Select));
  Multiplexer #(.enable("false")) multiplexer_3 (.in0(Input[6]), .in1(Input[4]), .out(Output[5]), .sel(Select));
  Multiplexer #(.enable("false")) multiplexer_4 (.in0(Input[5]), .in1(Input[3]), .out(Output[4]), .sel(Select));
  Multiplexer #(.enable("false")) multiplexer_5 (.in0(Input[4]), .in1(Input[2]), .out(Output[3]), .sel(Select));
  Multiplexer #(.enable("false")) multiplexer_6 (.in0(Input[3]), .in1(Input[1]), .out(Output[2]), .sel(Select));
  Multiplexer #(.enable("false")) multiplexer_7 (.in0(Input[2]), .in1(Input[0]), .out(Output[1]), .sel(Select));
  Multiplexer #(.enable("false")) multiplexer_8 (.in0(Input[1]), .in1(SHL), .out(Output[0]), .sel(Select));

  // Notes on the sheet:
  //   Select 0 : Right shift
  //   Select 1 : Left shift
  //   23CS041
endmodule

module _1_bit_ALU (
  input  B1,
  input  A1,
  input  CIN,
  input  [1:0] S1S0,
  input  [1:0] S3S2,
  input  A1_SHR,
  input  A1_SHL,
  output S0,
  output COUT,
  output O0,
  output E0
);

  _1_bit_arithmetic u_1_bit_arithmetic_1 (.Cin(CIN), .A0(A1), .B0(B1), .S1S0(S1S0), .S0(S0), .Cout(COUT));
  _1_bit_logical u_1_bit_logical_1 (.B0(B1), .A0(A1), .E0(E0), .S1S0(S1S0));
  Multiplexer #(.select(2), .enable("false")) multiplexer_1 (
    .in0(S0), .in1(E0), .in2(A1_SHR), .in3(A1_SHL), .out(O0), .sel(S3S2));

  // Notes on the sheet:
  //   23CS041
  //   1 BIT ALU
endmodule

module _2_bit_ALU (
  input  [1:0] A1A0,
  input  [1:0] B1B0,
  input  CIN,
  input  SHL,
  input  [1:0] S1S0,
  input  [1:0] S3S2,
  input  SHR,
  output S0,
  output COUT,
  output [1:0] F0F1,
  output S1,
  output COUT_2
);

  wire n1_bit_logical_1_e0, n1_bit_logical_2_e0;

  _1_bit_arithmetic u_1_bit_arithmetic_1 (.Cin(CIN), .A0(A1A0[0]), .B0(B1B0[0]), .S1S0(S1S0), .S0(S0), .Cout(COUT));
  _1_bit_logical u_1_bit_logical_1 (.B0(B1B0[0]), .A0(A1A0[0]), .E0(n1_bit_logical_1_e0), .S1S0(S1S0));
  _1_bit_arithmetic u_1_bit_arithmetic_2 (.Cin(S0), .A0(A1A0[1]), .B0(B1B0[1]), .S1S0(S1S0), .S0(S1), .Cout(COUT_2));
  _1_bit_logical u_1_bit_logical_2 (.B0(B1B0[1]), .A0(A1A0[1]), .E0(n1_bit_logical_2_e0), .S1S0(S3S2));
  Multiplexer #(.select(2), .enable("false")) multiplexer_1 (
    .in0(S0), .in1(n1_bit_logical_1_e0), .in2(A1A0[1]), .in3(SHL), .out(F0F1[0]), .sel(S3S2));
  Multiplexer #(.select(2), .enable("false")) multiplexer_2 (
    .in0(S1), .in1(n1_bit_logical_2_e0), .in2(SHR), .in3(A1A0[0]), .out(F0F1[1]), .sel(S3S2));

  // Notes on the sheet:
  //   23CS041
  //   BIT 0
  //   BIT 1
  //   2 BIT ALU
endmodule

module _4__bit_ALU (
  input  [3:0] B3B2B1B0,
  input  [3:0] A3A2A1A0,
  input  [3:0] S3S2S1S0,
  input  IR,
  input  IL,
  input  Cin,
  output [3:0] Output,
  output out_8,
  output out_9,
  output out_10,
  output out_11,
  output out_12,
  output out_13,
  output out_14,
  output out_15,
  output out_16
);

  wire n1_bit_arithmetic_1_cout, n1_bit_arithmetic_2_cout, n1_bit_arithmetic_3_cout;

  _1_bit_arithmetic u_1_bit_arithmetic_1 (
    .Cin(Cin), .A0(A3A2A1A0[0]), .B0(B3B2B1B0[0]), .S1S0(S3S2S1S0[1:0]), .S0(out_9),
    .Cout(n1_bit_arithmetic_1_cout));
  _1_bit_logical u_1_bit_logical_1 (.B0(B3B2B1B0[0]), .A0(A3A2A1A0[0]), .E0(out_10), .S1S0(S3S2S1S0[1:0]));
  _1_bit_arithmetic u_1_bit_arithmetic_2 (
    .Cin(n1_bit_arithmetic_1_cout), .A0(A3A2A1A0[1]), .B0(B3B2B1B0[1]), .S1S0(S3S2S1S0[1:0]), .S0(out_11),
    .Cout(n1_bit_arithmetic_2_cout));
  _1_bit_logical u_1_bit_logical_2 (.B0(B3B2B1B0[1]), .A0(A3A2A1A0[1]), .E0(out_12), .S1S0(S3S2S1S0[1:0]));
  _1_bit_arithmetic u_1_bit_arithmetic_3 (
    .Cin(n1_bit_arithmetic_2_cout), .A0(A3A2A1A0[2]), .B0(B3B2B1B0[2]), .S1S0(S3S2S1S0[1:0]), .S0(out_13),
    .Cout(n1_bit_arithmetic_3_cout));
  _1_bit_logical u_1_bit_logical_3 (.B0(B3B2B1B0[2]), .A0(A3A2A1A0[2]), .E0(out_14), .S1S0(S3S2S1S0[1:0]));
  _1_bit_arithmetic u_1_bit_arithmetic_4 (
    .Cin(n1_bit_arithmetic_3_cout), .A0(A3A2A1A0[3]), .B0(B3B2B1B0[3]), .S1S0(S3S2S1S0[1:0]), .S0(out_15),
    .Cout(out_8));
  _1_bit_logical u_1_bit_logical_4 (.B0(B3B2B1B0[3]), .A0(A3A2A1A0[3]), .E0(out_16), .S1S0(S3S2S1S0[1:0]));
  Multiplexer #(.select(2), .enable("false")) multiplexer_1 (
    .in0(out_9), .in1(out_10), .in2(IL), .in3(A3A2A1A0[0]), .out(Output[0]), .sel(S3S2S1S0[3:2]));
  Multiplexer #(.select(2), .enable("false")) multiplexer_2 (
    .in0(out_11), .in1(out_12), .in2(A3A2A1A0[0]), .in3(A3A2A1A0[1]), .out(Output[1]), .sel(S3S2S1S0[3:2]));
  Multiplexer #(.select(2), .enable("false")) multiplexer_3 (
    .in0(out_13), .in1(out_14), .in2(A3A2A1A0[1]), .in3(A3A2A1A0[2]), .out(Output[2]), .sel(S3S2S1S0[3:2]));
  Multiplexer #(.select(2), .enable("false")) multiplexer_4 (
    .in0(out_15), .in1(out_16), .in2(A3A2A1A0[2]), .in3(IR), .out(Output[3]), .sel(S3S2S1S0[3:2]));

  // Notes on the sheet:
  //   23CS041
  //   4 BIT ALU
  //   BIT0
  //   BIT1
  //   BIT2
  //   BIT3
endmodule

module _8_bit_ALU (
  input  [3:0] S3S2S1S0,
  input  SHL,
  input  [7:0] A7A6A5A4A3A2A1A0,
  input  CIN,
  input  [7:0] B7B6B5B4B2B1B0,
  input  SHR,
  output [7:0] S1,
  output S1_2,
  output S1_3,
  output S1_4,
  output S1_5,
  output S1_6,
  output S1_7,
  output S1_8,
  output S1_9,
  output COUT
);

  wire n1_bit_arithmetic_1_cout, n1_bit_arithmetic_3_cout, n1_bit_arithmetic_4_cout,
       n1_bit_arithmetic_5_cout, n1_bit_arithmetic_6_cout, n1_bit_arithmetic_7_cout, n1_bit_logical_1_e0,
       n1_bit_logical_2_e0, n1_bit_logical_3_e0, n1_bit_logical_4_e0, n1_bit_logical_5_e0,
       n1_bit_logical_6_e0, n1_bit_logical_7_e0, n1_bit_logical_8_e0;

  _1_bit_arithmetic u_1_bit_arithmetic_1 (
    .Cin(CIN), .A0(A7A6A5A4A3A2A1A0[0]), .B0(B7B6B5B4B2B1B0[0]), .S1S0(S3S2S1S0[1:0]), .S0(S1_2),
    .Cout(n1_bit_arithmetic_1_cout));
  _1_bit_logical u_1_bit_logical_1 (
    .B0(B7B6B5B4B2B1B0[0]), .A0(A7A6A5A4A3A2A1A0[0]), .E0(n1_bit_logical_1_e0), .S1S0(S3S2S1S0[1:0]));
  _1_bit_arithmetic u_1_bit_arithmetic_2 (
    .Cin(n1_bit_arithmetic_1_cout), .A0(A7A6A5A4A3A2A1A0[1]), .B0(B7B6B5B4B2B1B0[1]), .S1S0(S3S2S1S0[1:0]),
    .S0(S1_3), .Cout(S1_3));
  _1_bit_logical u_1_bit_logical_2 (
    .B0(B7B6B5B4B2B1B0[1]), .A0(A7A6A5A4A3A2A1A0[1]), .E0(n1_bit_logical_2_e0), .S1S0(S3S2S1S0[1:0]));
  _1_bit_arithmetic u_1_bit_arithmetic_3 (
    .Cin(S1_3), .A0(A7A6A5A4A3A2A1A0[4]), .B0(B7B6B5B4B2B1B0[2]), .S1S0(S3S2S1S0[1:0]), .S0(S1_4),
    .Cout(n1_bit_arithmetic_3_cout));
  _1_bit_logical u_1_bit_logical_3 (
    .B0(B7B6B5B4B2B1B0[2]), .A0(A7A6A5A4A3A2A1A0[4]), .E0(n1_bit_logical_3_e0), .S1S0(S3S2S1S0[1:0]));
  _1_bit_arithmetic u_1_bit_arithmetic_4 (
    .Cin(n1_bit_arithmetic_3_cout), .A0(A7A6A5A4A3A2A1A0[3]), .B0(B7B6B5B4B2B1B0[3]), .S1S0(S3S2S1S0[1:0]),
    .S0(S1_5), .Cout(n1_bit_arithmetic_4_cout));
  _1_bit_logical u_1_bit_logical_4 (
    .B0(B7B6B5B4B2B1B0[3]), .A0(A7A6A5A4A3A2A1A0[3]), .E0(n1_bit_logical_4_e0), .S1S0(S3S2S1S0[1:0]));
  _1_bit_arithmetic u_1_bit_arithmetic_5 (
    .Cin(n1_bit_arithmetic_4_cout), .A0(A7A6A5A4A3A2A1A0[4]), .B0(B7B6B5B4B2B1B0[4]), .S1S0(S3S2S1S0[1:0]),
    .S0(S1_6), .Cout(n1_bit_arithmetic_5_cout));
  _1_bit_logical u_1_bit_logical_5 (
    .B0(B7B6B5B4B2B1B0[4]), .A0(A7A6A5A4A3A2A1A0[4]), .E0(n1_bit_logical_5_e0), .S1S0(S3S2S1S0[1:0]));
  _1_bit_arithmetic u_1_bit_arithmetic_6 (
    .Cin(n1_bit_arithmetic_5_cout), .A0(A7A6A5A4A3A2A1A0[5]), .B0(B7B6B5B4B2B1B0[5]), .S1S0(S3S2S1S0[1:0]),
    .S0(S1_7), .Cout(n1_bit_arithmetic_6_cout));
  _1_bit_logical u_1_bit_logical_6 (
    .B0(B7B6B5B4B2B1B0[5]), .A0(A7A6A5A4A3A2A1A0[5]), .E0(n1_bit_logical_6_e0), .S1S0(S3S2S1S0[1:0]));
  _1_bit_arithmetic u_1_bit_arithmetic_7 (
    .Cin(n1_bit_arithmetic_6_cout), .A0(A7A6A5A4A3A2A1A0[6]), .B0(B7B6B5B4B2B1B0[6]), .S1S0(S3S2S1S0[1:0]),
    .S0(S1_8), .Cout(n1_bit_arithmetic_7_cout));
  _1_bit_logical u_1_bit_logical_7 (
    .B0(B7B6B5B4B2B1B0[6]), .A0(A7A6A5A4A3A2A1A0[6]), .E0(n1_bit_logical_7_e0), .S1S0(S3S2S1S0[1:0]));
  _1_bit_arithmetic u_1_bit_arithmetic_8 (
    .Cin(n1_bit_arithmetic_7_cout), .A0(A7A6A5A4A3A2A1A0[7]), .B0(B7B6B5B4B2B1B0[7]), .S1S0(S3S2S1S0[1:0]),
    .S0(S1_9), .Cout(COUT));
  _1_bit_logical u_1_bit_logical_8 (
    .B0(B7B6B5B4B2B1B0[7]), .A0(A7A6A5A4A3A2A1A0[7]), .E0(n1_bit_logical_8_e0), .S1S0(S3S2S1S0[1:0]));
  Multiplexer #(.select(2), .enable("false")) multiplexer_1 (
    .in0(S1_2), .in1(n1_bit_logical_1_e0), .in2(A7A6A5A4A3A2A1A0[1]), .in3(SHL), .out(S1[0]),
    .sel(S3S2S1S0[3:2]));
  Multiplexer #(.select(2), .enable("false")) multiplexer_2 (
    .in0(S1_3), .in1(n1_bit_logical_2_e0), .in2(A7A6A5A4A3A2A1A0[4]), .in3(A7A6A5A4A3A2A1A0[0]), .out(S1[1]),
    .sel(S3S2S1S0[3:2]));
  Multiplexer #(.select(2), .enable("false")) multiplexer_3 (
    .in0(S1_4), .in1(n1_bit_logical_3_e0), .in2(A7A6A5A4A3A2A1A0[3]), .in3(A7A6A5A4A3A2A1A0[1]), .out(S1[2]),
    .sel(S3S2S1S0[3:2]));
  Multiplexer #(.select(2), .enable("false")) multiplexer_4 (
    .in0(S1_5), .in1(n1_bit_logical_4_e0), .in2(A7A6A5A4A3A2A1A0[4]), .in3(A7A6A5A4A3A2A1A0[4]), .out(S1[3]),
    .sel(S3S2S1S0[3:2]));
  Multiplexer #(.select(2), .enable("false")) multiplexer_5 (
    .in0(S1_6), .in1(n1_bit_logical_5_e0), .in2(A7A6A5A4A3A2A1A0[5]), .in3(A7A6A5A4A3A2A1A0[3]), .out(S1[4]),
    .sel(S3S2S1S0[3:2]));
  Multiplexer #(.select(2), .enable("false")) multiplexer_6 (
    .in0(S1_7), .in1(n1_bit_logical_6_e0), .in2(A7A6A5A4A3A2A1A0[6]), .in3(A7A6A5A4A3A2A1A0[4]), .out(S1[5]),
    .sel(S3S2S1S0[3:2]));
  Multiplexer #(.select(2), .enable("false")) multiplexer_7 (
    .in0(S1_8), .in1(n1_bit_logical_7_e0), .in2(A7A6A5A4A3A2A1A0[7]), .in3(A7A6A5A4A3A2A1A0[5]), .out(S1[6]),
    .sel(S3S2S1S0[3:2]));
  Multiplexer #(.select(2), .enable("false")) multiplexer_8 (
    .in0(S1_9), .in1(n1_bit_logical_8_e0), .in2(SHR), .in3(A7A6A5A4A3A2A1A0[6]), .out(S1[7]),
    .sel(S3S2S1S0[3:2]));

  assign A7A6A5A4A3A2A1A0[2] = A7A6A5A4A3A2A1A0[4];

  // Notes on the sheet:
  //   23CS041
  //   8 BIT ALU
endmodule
