// Logisim project hw3_1.circ as structural Verilog: 1 circuit, main circuit main
module main (
  input  [2:0] Select,
  input  [3:0] Input_for_register_E,
  input  [3:0] Input_for_register_D,
  input  [3:0] Input_for_register_C,
  input  [3:0] Input_for_register_B,
  input  [3:0] Input_for_register_A,
  input  CLR,
  output [3:0] Coman_Bus,
  output [3:0] out_9,
  output [3:0] out_10,
  output [3:0] out_11,
  output [3:0] out_12,
  output [3:0] out_13
);

  wire clock_1_out;

  Clock clock_1 (.out(clock_1_out));
  Register #(.width(4)) Register_E (.D(Input_for_register_E), .en(1'b1), .Q(out_9), .clk(clock_1_out), .clr(CLR));
  Multiplexer #(.select(3), .enable("false")) multiplexer_1 (
    .in0(out_13[3]), .in1(out_12[3]), .in2(out_11[3]), .in3(out_10[3]), .in4(out_9[3]), .out(Coman_Bus[3]),
    .sel(Select));  // open: in5, in6, in7
  Register #(.width(4)) Register_D (.D(Input_for_register_D), .en(1'b1), .Q(out_10), .clk(clock_1_out), .clr(CLR));
  Multiplexer #(.select(3), .enable("false")) multiplexer_2 (
    .in0(out_13[2]), .in1(out_12[2]), .in2(out_11[2]), .in3(out_10[2]), .in4(out_9[2]), .out(Coman_Bus[2]),
    .sel(Select));  // open: in5, in6, in7
  Register #(.width(4)) Register_C (.D(Input_for_register_C), .en(1'b1), .Q(out_11), .clk(clock_1_out), .clr(CLR));
  Multiplexer #(.select(3), .enable("false")) multiplexer_3 (
    .in0(out_13[1]), .in1(out_12[1]), .in2(out_11[1]), .in3(out_10[1]), .in4(out_9[1]), .out(Coman_Bus[1]),
    .sel(Select));  // open: in5, in6, in7
  Register #(.width(4)) Register_B (.D(Input_for_register_B), .en(1'b1), .Q(out_12), .clk(clock_1_out), .clr(CLR));
  Multiplexer #(.select(3), .enable("false")) multiplexer_4 (
    .in0(out_13[0]), .in1(out_12[0]), .in2(out_11[0]), .in3(out_10[0]), .in4(out_9[0]), .out(Coman_Bus[0]),
    .sel(Select));  // open: in5, in6, in7
  Register #(.width(4)) Register_A (.D(Input_for_register_A), .en(1'b1), .Q(out_13), .clk(clock_1_out), .clr(CLR));

  // Notes on the sheet:
  //   Select 000 : A
  //   Select 001 : B
  //   Select 010 : C
  //   Select 011 : D
  //   Select 100 : E
  //   23CS041
  //   Bit 3
  //   Bit 2
  //   Bit 1
  //   Bit 0
endmodule
