// Logisim project hw3_2.circ as structural Verilog: 1 circuit, main circuit main
module main (
  input  [2:0] Select,
  input  [3:0] Input_for_register_E,
  input  [3:0] Input_for_register_D,
  input  [3:0] Input_for_register_C,
  input  [3:0] Input_for_register_B,
  input  [3:0] Input_for_register_A,
  input  CLR,
  output [3:0] Coman_Bus,
  output [3:0] out_9,
  output [3:0] out_10,
  output [3:0] out_11,
  output [3:0] out_12,
  output [3:0] out_13
);

  wire clock_1_out, decoder_1_out0, decoder_1_out1, decoder_1_out2, decoder_1_out3, decoder_1_out4;

  Clock clock_1 (.out(clock_1_out));
  Decoder #(.select(3)) decoder_1 (
    .out0(decoder_1_out0), .out1(decoder_1_out1), .out2(decoder_1_out2), .out3(decoder_1_out3),
    .out4(decoder_1_out4), .sel(Select));  // open: out5, out6, out7, en
  Register #(.width(4)) Register_E (.D(Input_for_register_E), .en(1'b1), .Q(out_9), .clk(clock_1_out), .clr(CLR));
  assign Coman_Bus[3] = decoder_1_out0 ? out_13[3] : 1'bz;  // Controlled_Buffer controlled_buffer_1
  assign Coman_Bus[3] = decoder_1_out1 ? out_12[3] : 1'bz;  // Controlled_Buffer controlled_buffer_2
  assign Coman_Bus[3] = decoder_1_out2 ? out_11[3] : 1'bz;  // Controlled_Buffer controlled_buffer_3
  assign Coman_Bus[3] = decoder_1_out3 ? out_10[3] : 1'bz;  // Controlled_Buffer controlled_buffer_4
  assign Coman_Bus[3] = decoder_1_out4 ? out_9[3] : 1'bz;  // Controlled_Buffer controlled_buffer_5
  Register #(.width(4)) Register_D (.D(Input_for_register_D), .en(1'b1), .Q(out_10), .clk(clock_1_out), .clr(CLR));
  assign Coman_Bus[2] = decoder_1_out0 ? out_13[2] : 1'bz;  // Controlled_Buffer controlled_buffer_6
  assign Coman_Bus[2] = decoder_1_out1 ? out_12[2] : 1'bz;  // Controlled_Buffer controlled_buffer_7
  assign Coman_Bus[2] = decoder_1_out2 ? out_11[2] : 1'bz;  // Controlled_Buffer controlled_buffer_8
  assign Coman_Bus[2] = decoder_1_out3 ? out_10[2] : 1'bz;  // Controlled_Buffer controlled_buffer_9
  assign Coman_Bus[2] = decoder_1_out4 ? out_9[2] : 1'bz;  // Controlled_Buffer controlled_buffer_10
  assign Coman_Bus[1] = decoder_1_out0 ? out_13[1] : 1'bz;  // Controlled_Buffer controlled_buffer_11
  assign Coman_Bus[1] = decoder_1_out1 ? out_12[1] : 1'bz;  // Controlled_Buffer controlled_buffer_12
  assign Coman_Bus[1] = decoder_1_out2 ? out_11[1] : 1'bz;  // Controlled_Buffer controlled_buffer_13
  assign Coman_Bus[1] = decoder_1_out3 ? out_10[1] : 1'bz;  // Controlled_Buffer controlled_buffer_14
  assign Coman_Bus[1] = decoder_1_out4 ? out_9[1] : 1'bz;  // Controlled_Buffer controlled_buffer_15
  Register #(.width(4)) Register_C (.D(Input_for_register_C), .en(1'b1), .Q(out_11), .clk(clock_1_out), .clr(CLR));
  assign Coman_Bus[0] = decoder_1_out0 ? out_13[0] : 1'bz;  // Controlled_Buffer controlled_buffer_16
  assign Coman_Bus[0] = decoder_1_out1 ? out_12[0] : 1'bz;  // Controlled_Buffer controlled_buffer_17
  assign Coman_Bus[0] = decoder_1_out2 ? out_11[0] : 1'bz;  // Controlled_Buffer controlled_buffer_18
  assign Coman_Bus[0] = decoder_1_out3 ? out_10[0] : 1'bz;  // Controlled_Buffer controlled_buffer_19
  assign Coman_Bus[0] = decoder_1_out4 ? out_9[0] : 1'bz;  // Controlled_Buffer controlled_buffer_20
  Register #(.width(4)) Register_B (.D(Input_for_register_B), .en(1'b1), .Q(out_12), .clk(clock_1_out), .clr(CLR));
  Register #(.width(4)) Register_A (.D(Input_for_register_A), .en(1'b1), .Q(out_13), .clk(clock_1_out), .clr(CLR));

  // Notes on the sheet:
  //   Select 000 : A
  //   Select 001 : B
  //   Select 010 : C
  //   Select 011 : D
  //   Select 100 : E
  //   Register A
  //   A3
  //   B3
  //   C3
  //   D3
  //   E3
  //   A2
  //   B2
  //   C2
  //   D2
  //   E2
  //   A1
  //   B1
  //   C1
  //   D1
  //   E1
  //   A0
  //   B0
  //   C0
  //   D0
  //   E0
  //   23CS041
endmodule
